# Fritzing sketch pcb (saved by Fritzing 0.9.3b)
circuit board: 8.46667cm x 5.64444cm
breadboards: 1

parts:
  IC1 = H-Bridge [package=THT]
  VCC1 = Battery block 9V

nets:
  N1: IC1.1_2EN, IC1.3_4EN
  GND1: IC1.GND1, IC1.GND2, IC1.GND3, IC1.GND4, VCC1.-
  N2: IC1.VCC2, VCC1.+
